// Logisim project ExpansionPort.circ as structural Verilog: 1 circuit, main circuit main
module main (
  input  nRD,
  input  nWR,
  input  MEM__IO,
  input  nINTA,
  input  nINT,
  output nIORQ,
  output nM1,
  output INTR
);

  wire nand_1_out, nand_2_out, nand_3_out;

  not not_1 (INTR, nINT);
  nand nand_1 (nand_1_out, nRD, nWR);
  nand nand_2 (nand_2_out, nand_1_out, MEM__IO);
  nand nand_3 (nand_3_out, nand_2_out, nINTA);
  nand nand_4 (nIORQ, nand_3_out, nand_3_out);

  assign nM1 = nINTA;

  // Notes on the sheet:
  //   8085
  //   EXP
endmodule
