// Logisim project A64CPM.circ as structural Verilog: 1 circuit, main circuit main
module main (
  input  nMEMRQ,
  input  A15,
  input  nWR,
  input  Ax,
  input  nIORQ,
  input  D0,
  input  nRD,
  input  in_8,
  output out_9,
  output nLOWRAMWRITE,
  output ROMSUPRESS,
  output nLOWRAMREAD
);

  wire d_ff_1_qn, or_1_out;

  or or_1 (or_1_out, Ax, nIORQ);
  or or_2 (out_9, nMEMRQ, A15);
  D_Flip_Flop d_ff_1 (.clk(or_1_out), .D(D0), .Q(ROMSUPRESS), .Qn(d_ff_1_qn), .reset(in_8));  // open: preset
  or or_3 (nLOWRAMREAD, d_ff_1_qn, nRD);

  assign nLOWRAMWRITE = nWR;

  // Notes on the sheet:
  //   #RESET
  //   #LOWRAMENABLE
endmodule
