// Logisim project A64memoryDecoding.circ as structural Verilog: 1 circuit, main circuit main
module main (
  input  A15,
  input  MEMRQ,
  output ROMSEL,
  output RAMSEL
);

  wire nand_1_out, nand_2_out;

  nand nand_1 (nand_1_out, A15, A15);
  nand nand_2 (nand_2_out, MEMRQ, MEMRQ);
  nand nand_3 (ROMSEL, nand_1_out, nand_2_out);
  nand nand_4 (RAMSEL, nand_2_out, A15);
endmodule
