// Logisim project Aniol64keyboard.circ as structural Verilog: 1 circuit, main circuit main
module main (
  input  in_1,
  input  IEI,
  input  RD,
  input  IORQ,
  input  D0,
  input  A6,
  input  WR,
  input  M1,
  input  RESET,
  input  IORQ_2,
  output IEO,
  output [6:0] D6_D0,
  output INT
);

  wire and_1_out, and_2_out, and_3_out, clock_1_out, d_ff_1_q, d_ff_2_q, d_ff_2_qn, not_3_out, not_4_out,
       not_5_out, or_1_out, or_2_out, or_3_out, or_4_out, or_5_out, pull_resistor_1_node,
       pull_resistor_2_node, pull_resistor_3_node, switch_3_p1, switch_3_p2;
  wire [4:0] counter_1_q;
  wire [6:0] register_1_q;
  wire [6:5] not_1_out;

  Pull_Resistor #(.pull(1)) pull_resistor_1 (.node(pull_resistor_1_node));
  // Switch switch_1: pin names not known; wires that end beside it: 1'b0, pull_resistor_1_node
  Pull_Resistor #(.pull(1)) pull_resistor_2 (.node(pull_resistor_2_node));
  // Switch switch_2: pin names not known; wires that end beside it: 1'b0, pull_resistor_2_node
  Clock clock_1 (.out(clock_1_out));
  Pull_Resistor pull_resistor_3 (.node(pull_resistor_3_node));
  not not_1 (not_1_out[5], pull_resistor_1_node);
  not not_2 (not_1_out[6], pull_resistor_2_node);
  or or_1 (or_1_out, IORQ, A6);
  Counter #(.max('h1f), .width(5)) counter_1 (
    .clr(in_1), .clk(or_2_out), .Q(counter_1_q));  // open: load, up, count, D, carry
  or or_2 (or_2_out, clock_1_out, pull_resistor_3_node);
  or or_3 (or_3_out, RD, or_1_out);
  or or_4 (or_4_out, or_1_out, WR);
  Register #(.width(7)) register_1 (.D({not_1_out, counter_1_q}), .clk(and_3_out), .Q(register_1_q));  // open: en, clr
  not not_3 (not_3_out, or_4_out);
  assign D6_D0 = not_4_out ? register_1_q : 7'bz;  // Controlled_Buffer controlled_buffer_1
  not not_4 (not_4_out, or_3_out);
  D_Flip_Flop d_ff_1 (.D(D0), .clk(not_3_out), .Q(d_ff_1_q));  // open: Qn, preset, reset
  Multiplexer #(.enable("false"), .select(2)) multiplexer_1 (
    .in0(switch_3_p2), .out(pull_resistor_3_node), .sel(counter_1_q[4:3]));  // open: in1, in2, in3
  LED led_1 (.in(pull_resistor_3_node));
  // Switch switch_3: pin names not known; wires that end beside it: switch_3_p1, switch_3_p2
  and and_1 (and_1_out, pull_resistor_3_node, IEI);
  // Buzzer buzzer_1: pin names not known; wires that end beside it: d_ff_1_q
  or or_5 (or_5_out, M1, IORQ_2);
  Demultiplexer #(.enable("false"), .select(3)) demultiplexer_1 (
    .out1(switch_3_p1), .in(1'b1), .sel(counter_1_q[2:0]));  // open: out0, out2, out3, out4, out5, out6, out7
  D_Flip_Flop d_ff_2 (.D(1'b1), .clk(and_1_out), .Q(d_ff_2_q), .Qn(d_ff_2_qn), .reset(not_5_out));  // open: preset
  not not_5 (not_5_out, and_2_out);
  and and_2 (and_2_out, or_5_out, RESET);
  and and_3 (and_3_out, d_ff_2_q, IEI);
  and and_4 (IEO, d_ff_2_qn, IEI);
  not not_6 (INT, and_3_out);

  // Notes on the sheet:
  //   ALT
  //   SHIFT
  //   Register OE'
  //   Interrupt Acknowledge
endmodule
