// Logisim project soundCardInterrupts.circ as structural Verilog: 1 circuit, main circuit main
module main (
  input  in_1,
  input  IORQ,
  input  M1,
  output [7:0] out_4
);

  wire clock_1_out, or_1_out, or_2_out;
  wire [7:0] pull_resistor_1_node;

  or or_1 (or_1_out, in_1, or_2_out);
  or or_2 (or_2_out, IORQ, M1);
  Pull_Resistor pull_resistor_1 (.node(pull_resistor_1_node[0]));
  Pull_Resistor pull_resistor_2 (.node(pull_resistor_1_node[1]));
  Pull_Resistor pull_resistor_3 (.node(pull_resistor_1_node[2]));
  Pull_Resistor #(.pull(1)) pull_resistor_4 (.node(pull_resistor_1_node[3]));
  Pull_Resistor pull_resistor_5 (.node(pull_resistor_1_node[4]));
  Pull_Resistor pull_resistor_6 (.node(pull_resistor_1_node[5]));
  Pull_Resistor pull_resistor_7 (.node(pull_resistor_1_node[6]));
  Pull_Resistor pull_resistor_8 (.node(pull_resistor_1_node[7]));
  assign out_4 = or_1_out ? pull_resistor_1_node : 8'bz;  // Controlled_Buffer controlled_buffer_1
  Counter counter_1 (.clr(clock_1_out));  // open: load, up, count, clk, D, carry, Q
  Clock clock_1 (.out(clock_1_out));

  // Notes on the sheet:
  //   D0-D7
endmodule
