// Logisim project VGA.circ as structural Verilog: 1 circuit, main circuit main
module main (
  output VGA_out
);

  wire clock_1_out, counter_1_carry;
  wire [2:0] counter_2_q_2;
  wire [7:0] ram_1_dout;
  wire [8:0] counter_1_q;
  wire [10:6] counter_2_q;

  Clock clock_1 (.out(clock_1_out));
  Counter #(.max('h1ff), .width(9)) counter_1 (
    .clk(clock_1_out), .carry(counter_1_carry), .Q(counter_1_q));  // open: clr, load, up, count, D
  RAM #(.addrWidth(11)) ram_1 (.addr({counter_2_q, counter_1_q[8:3]}), .dout(ram_1_dout));  // open: we, oe, clk, din
  Counter counter_2 (.clk(counter_1_carry), .Q({counter_2_q, counter_2_q_2}));  // open: clr, load, up, count, D, carry
  ROM #(.addrWidth(11)) rom_1 (.addr({ram_1_dout, counter_2_q_2}));  // open: data
  // Shift_Register shift_register_1: pin names not known; wires that end beside it: clock_1_out, VGA_out

  // Notes on the sheet:
  //   X counter
  //   Image RAM
  //   Y counter
  //   Character ROM
endmodule
